# Fritzing sketch plowduino (saved by Fritzing 0.9.3b)
circuit board: 5.61346cm x 2.62946cm
breadboards: 1

parts:
  C7 = Ceramic Capacitor [capacitance=22pF rated_voltage=35V package="200 mil [THT, multilayer]"]
  C8 = Electrolytic Capacitor [capacitance=10µF rated_voltage=35V package="100 mil [THT, electrolytic]"]
  C9 = Electrolytic Capacitor [capacitance=10µF rated_voltage=35V package="100 mil [THT, electrolytic]"]
  U3 = Voltage Regulator - 5V [package="TO220 [THT]"]
  XTAL2 = Crystal [frequency="16 Mhz" package=THT]
  Power_plug2 = Power plug
  J6 = female pin header, 14 pins [form="♀ (female rounded)"]
  J7 = female pin header, 14 pins [form="♀ (female rounded)"]
  U4 = atmega168 [package=dip]
  C10 = Ceramic Capacitor [capacitance=22pF package="200 mil [THT, multilayer]"]  # not connected
  R3 = Resistor [tolerance=±5% resistance=1k package=THT]

nets (from the pcb view):
  N1: C7.0, XTAL2.pin_1, J6.pin10, U4.XLAT2
  N2: C7.1, J6.pin8, J7.pin7, U4.GND
  GND: C8.-, C9.+, U3.GND, Power_plug2.GND
  N3: C8.+, U3.input_voltage, Power_plug2.VCC
  N4: C9.-, U3.output_voltage, J6.pin7, J7.pin8, J7.pin9, U4.VCC, U4.AVCC, U4.AREF, R3.Pin_0
  N5: XTAL2.pin_0, J6.pin9, U4.XLAT1
  N6: J6.pin1, U4.RESET, R3.Pin_1
  N7: J6.pin2, U4.D0_(RX)
  N8: J6.pin3, U4.D1_(TX)
  N9: J6.pin4, U4.D2
  N10: J6.pin5, U4.D3_(PWM)
  N11: J6.pin6, U4.D4
  N12: J6.pin11, U4.D5_(PWM)
  N13: J6.pin12, U4.D6_(PWM)
  N14: J6.pin13, U4.D7
  N15: J6.pin14, U4.D8
  N16: J7.pin1, U4.A5
  N17: J7.pin2, U4.A4
  N18: J7.pin3, U4.A3
  N19: J7.pin4, U4.A2
  N20: J7.pin5, U4.A1
  N21: J7.pin6, U4.A0
  N22: J7.pin10, U4.D13
  N23: J7.pin11, U4.D12
  N24: J7.pin12, U4.D11_(PWM)
  N25: J7.pin13, U4.D10_(PWM)
  N26: J7.pin14, U4.D9_(PWM)

notes:
  This is a breadboard Arduino without an FTDI chip. You can program the chip with a USB-Serial breakout board, by using an external programmer or by programming the MCU in an Arduino board and then popping it into this circuit. The power source should be at least 7 VDC. Related example: http://itp.nyu.edu/physcomp/Tutorials/ArduinoBreadboard
